# Fritzing sketch sketch (saved by Fritzing 0.9.5d)
breadboards: 1

parts:
  Composant1 = Arduino Nano (Rev3.0)
  Composant2 = PN532 Elechouse RFID NFC Module V3
  U1 = FS1000A - 433Mhz RF Transmitter [package=THT]
  U3 = XD-RF-5V [package=THT]
  MCU1 = Raspberry Pi A+

nets:
  GND: Composant1.GND, Composant2.GND, U1.GND
  N1: Composant1.D12/MISO, U1.DATA
  VCC: Composant1.5V, Composant2.VCC, U1.VCC
  N2: Composant1.A5, Composant2.SCL
  N3: Composant1.A4, Composant2.SDA
  N4: U3.VCC, MCU1.pin_2
  N5: U3.DATA, MCU1.pin_13
  N6: U3.GND, MCU1.pin_6, MCU1.pin_9

custom parts:
  PN532 Elechouse RFID NFC Module V3: NFC is a popular technology in recent years. We often heard this work while smart phone company such as Samsung or HTC introduces their latest high-end phones. Almost all the high-end phone in the market support NFC. Near field communication (NFC) is a set of standards for smart phones and similar devices to establish radio communication with each other by touching them together or bringing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
  FS1000A - 433Mhz RF Transmitter: This is 433Mhz RF transmitter with receiver kit for Arduino ARM MCU wireless Application environment: Remote control switch, receiver module, motorcycles, automobile anti-theft products, home security products, electric doors, shutter doors, windows, remote control socket, remote control LED, remote audio remote control electric doors, garage door remote control, remote control retractable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
  XD-RF-5V: This is 433Mhz RF transmitter with receiver kit for Arduino ARM MCU wireless Application environment: Remote control switch, receiver module, motorcycles, automobile anti-theft products, home security products, electric doors, shutter doors, windows, remote control socket, remote control LED, remote audio remote control electric doors, garage door remote control, remote control retractable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
  Raspberry Pi A+: The awesome Raspberry Pi ARM Board with 40 pin GPIO. Ready for special designed Raspberry Pi A+ Hat (Hardware attached (on) top). Jan 2018: Cloned from the B+ version, and modified to match the official I/O pin numbers with a totally new schematic.
